# Fritzing sketch GY-530 VL53L0X LaserentfernungsmesserFitzing (saved by Fritzing 0.9.3b)

parts:
  Part1 = Adafruit VL53L0X Time of Flight Distance Sensor [part_number="Adafruit #3317"]
  Part2 = Arduino Leonardo (Rev3b)

nets:
  VIN: Part1.VIN, Part2.5V
  GND: Part1.GND, Part2.GND
  N1: Part1.GPIO, Part2.D7
  N2: Part1.SCL, Part2.SCL
  N3: Part1.SDA, Part2.SDA

custom parts:
  Adafruit VL53L0X Time of Flight Distance Sensor: The VL53L0X is a Time of Flight distance sensor like no other you've used! The sensor contains a very tiny invisible laser source, and a matching sensor. The VL53L0X can detect the "time of flight", or how long the light has taken to bounce back to the sensor. Since it uses a very narrow light source, it is good for determining distance of only the surface directly in front of it. Unlike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
