# Fritzing sketch AnschlussAnESP32 (saved by Fritzing 1.0.1rc)

parts:
  INA1 = INA219 DC Current Sensor Breakout
  U1 = ESP32-38PinWide [part_number=ESP32-38PinWide]
  LED1 = smd LED [color="Red (633nm)" package="0603 [SMD]"]
  R1 = Resistor [tolerance=±5% resistance=220 package="0603 [SMD]"]

nets:
  N1: INA1.VCC, INA1.Vin-, U1.3.3
  GND: INA1.GND, U1.GND, LED1.cathode
  N2: INA1.SCL, U1.GPIO23
  N3: INA1.SDA, U1.GPIO22
  N4: INA1.Vin+, R1.Pin_0
  N5: LED1.anode, R1.Pin_1

custom parts:
  INA219 DC Current Sensor Breakout: INA DC Current Sensor Breakout
  ESP32-38PinWide: Generic 38-Pin ESP32 with wide format (only access to one side of pins on a breadboard) based on Stephen Lilley's HiLetgo ESP-WROOM-32 ESP32 ESP-32S Development Board.
