# Fritzing sketch I2CLogicLevelConversion (saved by Fritzing 0.9.3b)

parts:
  LLC1 = Logic Level Converter [package="Breakout board"]
  M1 = DOIT Esp32 DevKit v1 (30 pins long, 11 pins width) [part_number=ESP32S-PIN30]
  Part1 = Arduino Leonardo (Rev3b)

nets:
  N1: LLC1.LV, M1.3V3
  N2: LLC1.L-GND, M1.D14, M1.GND
  N3: LLC1.LV3, M1.D22
  N4: LLC1.LV4, M1.D21
  N5: LLC1.HV4, Part1.D2/SDA
  N6: LLC1.HV3, Part1.D3_PWM/SCL
  N7: LLC1.H-GND, Part1.GND
  N8: LLC1.HV, Part1.5V

custom parts:
  Logic Level Converter: 5V to/from 3.3V logic level converter
  DOIT Esp32 DevKit v1 (30 pins long, 11 pins width): The DOIT Esp32 DevKit v1 is one of the development board created by DOIT to evaluate the ESP-WROOM-32 module. It is based on the ESP32 microcontroller that boasts Wifi, Bluetooth, Ethernet and Low Power support all in a single chip. (vanepp) made breadboard work, adjusted pin numbering and labels and reduced size of schematic and cleaned up pcb. This chip is 30pins long (2 x15) and 11 pins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
