# Fritzing sketch TFMiniChematicConnection (saved by Fritzing 0.9.3b)

parts:
  Part1 = Arduino Leonardo (Rev3b)
  Part2 = LIDAR-Lite

nets:
  N1: Part1.D0/RX, Part1.D1/TX, Part2.SCL, Part2.SDA
  5V: Part1.5V, Part2.5V, Part2.PWR_EN
  GND: Part1.GND, Part2.GND

notes:
  sda = RX
  sdc = TX

custom parts:
  LIDAR-Lite: PulsedLight LIDAR-Lite Sensor
